# Fritzing sketch micro-xbee-am2302 (saved by Fritzing 0.9.3b)
breadboards: 1

parts:
  Part1 = Arduino Micro (Rev3)
  Part3 = XBee USB Mini Adapter
  AM1 = AM2302 Humidity and Temperature Sensor

nets:
  N1: Part1.D1/TX, Part3.TXD
  N2: Part1.D0/RX, Part3.RXD
  GND: Part1.GND, Part3.GND, AM1.GND
  N3: Part1.D7, AM1.DATA
  5V: Part1.5V, Part3.5V, AM1.VDD
