# Fritzing sketch micro-xbee-bme280 (saved by Fritzing 0.9.3b)
breadboards: 1

parts:
  Part1 = Arduino Micro (Rev3)
  Part2 = BME280 Breakout
  Part3 = XBee USB Mini Adapter

nets:
  N1: Part1.D1/TX, Part3.TXD
  N2: Part1.D0/RX, Part3.RXD
  GND: Part1.GND, Part2.GND, Part3.GND
  N3: Part1.D2/SDA, Part2.SCK/SCL
  N4: Part1.D3/SCL, Part2.SDI/SDA
  5V: Part1.5V, Part3.5V
  3V3: Part1.3V3, Part2.3.3V
