# Fritzing sketch nano-xbee-bme280 (saved by Fritzing 0.9.3b)

parts:
  Part2 = BME280 Breakout
  Part3 = XBee USB Mini Adapter
  Part4 = Arduino Nano (Rev3.0)

nets:
  GND: Part2.GND, Part3.GND, Part4.GND
  3.3V: Part2.3.3V, Part4.3V3
  N1: Part2.SDI/SDA, Part4.A4
  N2: Part2.SCK/SCL, Part4.A5
  N3: Part3.RST, Part3.RXD, Part4.D0/RX
  N4: Part3.TXD, Part4.D1/TX
  5V: Part3.5V, Part4.5V
