# Fritzing sketch nano-xbee-dht22 (saved by Fritzing 0.9.3b)

parts:
  Part3 = XBee USB Mini Adapter
  DHT1 = DHT22 Humidity and Temperature Sensor
  R1 = Resistor [tolerance=±5% resistance=10k package="2512 [SMD]"]
  Part4 = Arduino Nano (Rev3.0)

nets:
  N1: Part3.RXD, Part4.D0/RX
  N2: Part3.TXD, Part4.D1/TX
  GND: Part3.GND, DHT1.GND, Part4.GND
  5V: Part3.5V, DHT1.VDD, Part4.5V
  N3: DHT1.DATA, R1.Pin_0, Part4.D7
